// Logisim project TalosES_CTRL_card.circ as structural Verilog: 1 circuit, main circuit CTRL
module CTRL (
  input  [7:0] OPCODEIMM,
  input  nHLT,
  input  nRST,
  input  SYSCLK,
  input  COMF,
  input  SIMF,
  input  CFH,
  input  SFH,
  input  ZFH,
  input  CFL,
  input  SFL,
  input  ZFL,
  output CLK,
  output OMF,
  output IMF,
  output out_16,
  output [7:0] IBH,
  output nRD,
  output nWR,
  output AHLE,
  output AR2LE,
  output IBLIOE,
  output SNL,
  output [7:0] IBL,
  output AHOE,
  output AR2OE,
  output JAHLE,
  output ALLE,
  output BHLE,
  output JALLE,
  output ALOE,
  output BHOE,
  output PCLE,
  output AR1CE,
  output BLLE,
  output RHOE,
  output AR1LE,
  output BLOE,
  output RLOE,
  output AR1OE,
  output EDBIE,
  output SFW,
  output AR2CE,
  output IBHIOE,
  output SNH
);

  wire CIMF, FREE, IMF_t, IMMHOE, IMMLOE, n7400_1_pin8, n7400_1_pin11, n7408_1_pin1, n7408_1_pin3,
       n7408_1_pin6, n7408_2_pin3, n7414_1_pin1, n7414_1_pin2, n7414_1_pin6, n7414_1_pin10, n7414_1_pin11,
       n7414_1_pin12, n7414_1_pin13, n7432_1_pin1, n7432_1_pin2, n7432_1_pin3, n7432_1_pin4, n7432_1_pin6,
       n7432_1_pin8, n7432_1_pin11, n7432_1_pin12, n7432_1_pin13, n7474_1_pin2, n7474_1_pin3, n7474_1_pin6,
       n7474_1_pin8, n7474_1_pin11, n7474_1_pin12, n7474_2_pin1, n7474_2_pin2, n7474_2_pin3, n7474_2_pin4,
       n7474_2_pin5, n7474_2_pin6, n7474_2_pin8, n7474_2_pin9, n7474_2_pin10, n7474_2_pin12, n7474_3_pin1,
       n7474_3_pin2, n7474_3_pin6, n7474_3_pin9, n7474_3_pin10, n74273_1_pin3, n74273_1_pin4, n74273_1_pin7,
       n74273_1_pin8, n74273_1_pin13, n74273_1_pin14, n74273_1_pin17, n74273_1_pin18, n74273_2_pin2,
       n74273_2_pin5, n74273_2_pin6, n74273_2_pin9, n74273_2_pin12, n74273_2_pin15, n74273_2_pin16,
       n74273_2_pin19, n74273_3_pin2, n74273_3_pin5, n74273_3_pin6, n74273_3_pin9, n74273_3_pin12,
       n74273_3_pin15, n74273_3_pin16, n74273_3_pin19, n74273_4_pin2, n74273_4_pin5, n74273_4_pin6,
       n74273_4_pin9, n74273_4_pin12, n74273_4_pin15, n74273_4_pin16, n74273_4_pin19, n74273_5_pin2,
       n74273_5_pin5, n74273_5_pin6, n74273_5_pin9, n74273_5_pin12, n74273_5_pin15, n74273_5_pin16,
       n74273_5_pin19, n74273_6_pin2, n74273_6_pin5, n74273_6_pin6, n74273_6_pin9, n74273_6_pin12,
       n74273_6_pin15, n74273_6_pin16, n74273_6_pin19, nCLK, nOE, nSYSCLK, OMF_t, pla_1_out, RD, SOMF, WR;
  wire [7:0] rom_1_data, rom_2_data, rom_3_data, rom_4_data;
  wire [15:8] n74273_1_pin2;

  _74273 u_74273_1 (
    .pin1(nRST), .pin2(n74273_1_pin2[8]), .pin3(n74273_1_pin3), .pin4(n74273_1_pin4),
    .pin5(n74273_1_pin2[9]), .pin6(n74273_1_pin2[10]), .pin7(n74273_1_pin7), .pin8(n74273_1_pin8),
    .pin9(n74273_1_pin2[11]), .pin19(n74273_1_pin2[15]), .pin18(n74273_1_pin18), .pin17(n74273_1_pin17),
    .pin16(n74273_1_pin2[14]), .pin15(n74273_1_pin2[13]), .pin14(n74273_1_pin14), .pin13(n74273_1_pin13),
    .pin12(n74273_1_pin2[12]), .pin11(nCLK));
  Pull_Resistor pull_resistor_1 (.node(n74273_1_pin3));
  Pull_Resistor pull_resistor_2 (.node(n74273_1_pin4));
  Pull_Resistor pull_resistor_3 (.node(n74273_1_pin7));
  Pull_Resistor pull_resistor_4 (.node(n74273_1_pin8));
  Pull_Resistor pull_resistor_5 (.node(n74273_1_pin13));
  Pull_Resistor pull_resistor_6 (.node(n74273_1_pin14));
  Pull_Resistor pull_resistor_7 (.node(n74273_1_pin17));
  Pull_Resistor pull_resistor_8 (.node(n74273_1_pin18));
  IC74245 ic74245_1 (
    .DIR(1'b0), .iOE(n7408_1_pin6), .B0(OPCODEIMM[0]), .B1(OPCODEIMM[1]), .B2(OPCODEIMM[2]),
    .B3(OPCODEIMM[3]), .B4(OPCODEIMM[4]), .B5(OPCODEIMM[5]), .B6(OPCODEIMM[6]), .B7(OPCODEIMM[7]),
    .A0(n74273_1_pin3), .A1(n74273_1_pin4), .A2(n74273_1_pin7), .A3(n74273_1_pin8), .A4(n74273_1_pin13),
    .A5(n74273_1_pin14), .A6(n74273_1_pin17), .A7(n74273_1_pin18));
  ROM #(.addrWidth(16)) rom_1 (.addr({n74273_1_pin2, OMF_t, IMF_t, CFH, CFL, SFH, SFL, ZFH, ZFL}), .data(rom_1_data));
  _74273 u_74273_2 (
    .pin1(nRST), .pin2(n74273_2_pin2), .pin3(rom_1_data[0]), .pin4(rom_1_data[1]), .pin5(n74273_2_pin5),
    .pin6(n74273_2_pin6), .pin7(rom_1_data[2]), .pin8(rom_1_data[3]), .pin9(n74273_2_pin9),
    .pin19(n74273_2_pin19), .pin18(rom_1_data[7]), .pin17(rom_1_data[6]), .pin16(n74273_2_pin16),
    .pin15(n74273_2_pin15), .pin14(rom_1_data[5]), .pin13(rom_1_data[4]), .pin12(n74273_2_pin12), .pin11(nCLK));
  Pull_Resistor pull_resistor_9 (.node(AHLE));
  Pull_Resistor pull_resistor_10 (.node(AHOE));
  Pull_Resistor pull_resistor_11 (.node(ALLE));
  Pull_Resistor pull_resistor_12 (.node(ALOE));
  Pull_Resistor pull_resistor_13 (.node(AR1CE));
  Pull_Resistor pull_resistor_14 (.node(AR1LE));
  Pull_Resistor pull_resistor_15 (.node(AR1OE));
  Pull_Resistor pull_resistor_16 (.node(AR2CE));
  _7432 u_7432_1 (
    .pin1(n7432_1_pin1), .pin2(n7432_1_pin2), .pin3(n7432_1_pin3), .pin4(n7432_1_pin4), .pin5(nRST),
    .pin6(n7432_1_pin6), .pin13(n7432_1_pin13), .pin12(n7432_1_pin12), .pin11(n7432_1_pin11), .pin10(nRST),
    .pin9(COMF), .pin8(n7432_1_pin8));
  // NoConnect on n7432_1_pin11
  // NoConnect on n7432_1_pin3
  IC74245 ic74245_2 (
    .DIR(1'b0), .iOE(nOE), .B0(n74273_2_pin19), .B1(n74273_2_pin16), .B2(n74273_2_pin15),
    .B3(n74273_2_pin12), .B4(n74273_2_pin9), .B5(n74273_2_pin6), .B6(n74273_2_pin5), .B7(n74273_2_pin2),
    .A0(AHLE), .A1(AHOE), .A2(ALLE), .A3(ALOE), .A4(AR1CE), .A5(AR1LE), .A6(AR1OE), .A7(AR2CE));
  // NoConnect on n7414_1_pin12
  _7414 u_7414_1 (
    .pin1(n7414_1_pin1), .pin2(n7414_1_pin2), .pin3(CIMF), .pin4(n7432_1_pin4), .pin5(SOMF),
    .pin6(n7414_1_pin6), .pin13(n7414_1_pin13), .pin12(n7414_1_pin12), .pin11(n7414_1_pin11),
    .pin10(n7414_1_pin10), .pin9(SYSCLK), .pin8(nSYSCLK));
  // NoConnect on n7414_1_pin2
  _7474 u_7474_1 (
    .pin1(n7432_1_pin6), .pin2(n7474_1_pin2), .pin3(n7474_1_pin3), .pin4(SIMF), .pin5(IMF),
    .pin6(n7474_1_pin6), .pin13(n7432_1_pin8), .pin12(n7474_1_pin12), .pin11(n7474_1_pin11),
    .pin10(n7414_1_pin6), .pin9(OMF), .pin8(n7474_1_pin8));
  ROM #(.addrWidth(16)) rom_2 (.addr({n74273_1_pin2, OMF_t, IMF_t, CFH, CFL, SFH, SFL, ZFH, ZFL}), .data(rom_2_data));
  // NoConnect on n7414_1_pin10
  // NoConnect on n7474_1_pin8
  // NoConnect on n7474_1_pin6
  _74273 u_74273_3 (
    .pin1(nRST), .pin2(n74273_3_pin2), .pin3(rom_2_data[0]), .pin4(rom_2_data[1]), .pin5(n74273_3_pin5),
    .pin6(n74273_3_pin6), .pin7(rom_2_data[2]), .pin8(rom_2_data[3]), .pin9(n74273_3_pin9),
    .pin19(n74273_3_pin19), .pin18(rom_2_data[7]), .pin17(rom_2_data[6]), .pin16(n74273_3_pin16),
    .pin15(n74273_3_pin15), .pin14(rom_2_data[5]), .pin13(rom_2_data[4]), .pin12(n74273_3_pin12), .pin11(nCLK));
  Pull_Resistor #(.pull(1)) pull_resistor_17 (.node(OMF));
  Pull_Resistor #(.pull(1)) pull_resistor_18 (.node(IMF));
  Pull_Resistor pull_resistor_19 (.node(AR2LE));
  Pull_Resistor pull_resistor_20 (.node(AR2OE));
  Pull_Resistor pull_resistor_21 (.node(BHLE));
  Pull_Resistor pull_resistor_22 (.node(BHOE));
  Pull_Resistor pull_resistor_23 (.node(BLLE));
  Pull_Resistor pull_resistor_24 (.node(BLOE));
  Pull_Resistor pull_resistor_25 (.node(EDBIE));
  Pull_Resistor pull_resistor_26 (.node(IBHIOE));
  IC74245 ic74245_3 (
    .DIR(1'b0), .iOE(nOE), .B0(n74273_3_pin19), .B1(n74273_3_pin16), .B2(n74273_3_pin15),
    .B3(n74273_3_pin12), .B4(n74273_3_pin9), .B5(n74273_3_pin6), .B6(n74273_3_pin5), .B7(n74273_3_pin2),
    .A0(AR2LE), .A1(AR2OE), .A2(BHLE), .A3(BHOE), .A4(BLLE), .A5(BLOE), .A6(EDBIE), .A7(IBHIOE));
  ROM #(.addrWidth(16)) rom_3 (.addr({n74273_1_pin2, OMF_t, IMF_t, CFH, CFL, SFH, SFL, ZFH, ZFL}), .data(rom_3_data));
  _7474 u_7474_2 (
    .pin1(n7474_2_pin1), .pin2(n7474_2_pin2), .pin3(n7474_2_pin3), .pin4(n7474_2_pin4), .pin5(n7474_2_pin5),
    .pin6(n7474_2_pin6), .pin13(nRST), .pin12(n7474_2_pin12), .pin11(nCLK), .pin10(n7474_2_pin10),
    .pin9(n7474_2_pin9), .pin8(n7474_2_pin8));
  _7474 u_7474_3 (
    .pin1(n7474_3_pin1), .pin2(n7474_3_pin2), .pin3(nSYSCLK), .pin4(nRST), .pin5(nOE), .pin6(n7474_3_pin6),
    .pin13(nRST), .pin12(nHLT), .pin11(SYSCLK), .pin10(n7474_3_pin10), .pin9(n7474_3_pin9),
    .pin8(n7474_3_pin2));
  // NoConnect on n7474_2_pin5
  // NoConnect on n7474_2_pin6
  _74273 u_74273_4 (
    .pin1(nRST), .pin2(n74273_4_pin2), .pin3(rom_3_data[0]), .pin4(rom_3_data[1]), .pin5(n74273_4_pin5),
    .pin6(n74273_4_pin6), .pin7(rom_3_data[2]), .pin8(rom_3_data[3]), .pin9(n74273_4_pin9),
    .pin19(n74273_4_pin19), .pin18(rom_3_data[7]), .pin17(rom_3_data[6]), .pin16(n74273_4_pin16),
    .pin15(n74273_4_pin15), .pin14(rom_3_data[5]), .pin13(rom_3_data[4]), .pin12(n74273_4_pin12), .pin11(nCLK));
  Pull_Resistor pull_resistor_27 (.node(IBLIOE));
  Pull_Resistor pull_resistor_28 (.node(JAHLE));
  Pull_Resistor pull_resistor_29 (.node(JALLE));
  Pull_Resistor pull_resistor_30 (.node(PCLE));
  Pull_Resistor pull_resistor_31 (.node(RHOE));
  Pull_Resistor pull_resistor_32 (.node(RLOE));
  Pull_Resistor pull_resistor_33 (.node(SFW));
  Pull_Resistor pull_resistor_34 (.node(SNH));
  PLA #(.in_width(8), .out_width(1), .\table ("00000001 1 # opcode = 1\n00000010 1 # opcode = 2\n00000011 1 # opcode = 3\n00000100 1 # opcode = 4\n00000101 1 # opcode = 5\n00000110 1 # opcode = 6")) pla_1 (
    .in(OPCODEIMM), .out(pla_1_out));
  _7408 u_7408_1 (
    .pin1(n7408_1_pin1), .pin2(n7408_1_pin1), .pin3(n7408_1_pin3), .pin4(n7408_1_pin3), .pin5(n7408_1_pin3),
    .pin6(n7408_1_pin6), .pin13(n7474_2_pin8), .pin12(pla_1_out), .pin11(n7474_2_pin12),
    .pin10(n7474_2_pin9), .pin9(n7474_2_pin9), .pin8(n7408_1_pin1));
  _7408 u_7408_2 (
    .pin1(nRST), .pin2(nRST), .pin3(n7408_2_pin3), .pin4(n7408_2_pin3), .pin5(n7408_2_pin3), .pin6(out_16),
    .pin13(n7474_3_pin9), .pin12(nSYSCLK), .pin11(nCLK), .pin10(SYSCLK), .pin9(n7474_3_pin6), .pin8(CLK));
  IC74245 ic74245_4 (
    .DIR(1'b0), .iOE(nOE), .B0(n74273_4_pin19), .B1(n74273_4_pin16), .B2(n74273_4_pin15),
    .B3(n74273_4_pin12), .B4(n74273_4_pin9), .B5(n74273_4_pin6), .B6(n74273_4_pin5), .B7(n74273_4_pin2),
    .A0(IBLIOE), .A1(JAHLE), .A2(JALLE), .A3(PCLE), .A4(RHOE), .A5(RLOE), .A6(SFW), .A7(SNH));
  Pull_Resistor #(.pull(1)) pull_resistor_35 (.node(out_16));
  ROM #(.addrWidth(16)) rom_4 (.addr({n74273_1_pin2, OMF_t, IMF_t, CFH, CFL, SFH, SFL, ZFH, ZFL}), .data(rom_4_data));
  _74273 u_74273_5 (
    .pin1(nRST), .pin2(n74273_5_pin2), .pin3(rom_4_data[0]), .pin4(rom_4_data[1]), .pin5(n74273_5_pin5),
    .pin6(n74273_5_pin6), .pin7(rom_4_data[2]), .pin8(rom_4_data[3]), .pin9(n74273_5_pin9),
    .pin19(n74273_5_pin19), .pin18(rom_4_data[7]), .pin17(rom_4_data[6]), .pin16(n74273_5_pin16),
    .pin15(n74273_5_pin15), .pin14(rom_4_data[5]), .pin13(rom_4_data[4]), .pin12(n74273_5_pin12), .pin11(nCLK));
  Pull_Resistor pull_resistor_36 (.node(SNL));
  Pull_Resistor pull_resistor_37 (.node(IMMHOE));
  Pull_Resistor pull_resistor_38 (.node(IMMLOE));
  Pull_Resistor pull_resistor_39 (.node(RD));
  Pull_Resistor pull_resistor_40 (.node(WR));
  Pull_Resistor pull_resistor_41 (.node(CIMF));
  Pull_Resistor pull_resistor_42 (.node(SOMF));
  Pull_Resistor pull_resistor_43 (.node(FREE));
  IC74245 ic74245_5 (
    .DIR(1'b0), .iOE(nOE), .B0(n74273_5_pin19), .B1(n74273_5_pin16), .B2(n74273_5_pin15),
    .B3(n74273_5_pin12), .B4(n74273_5_pin9), .B5(n74273_5_pin6), .B6(n74273_5_pin5), .B7(n74273_5_pin2),
    .A0(SNL), .A1(IMMHOE), .A2(IMMLOE), .A3(RD), .A4(WR), .A5(CIMF), .A6(SOMF), .A7(FREE));
  _7400 u_7400_1 (
    .pin1(RD), .pin2(RD), .pin3(nRD), .pin4(SYSCLK), .pin5(WR), .pin6(nWR), .pin13(IMMHOE), .pin12(IMMHOE),
    .pin11(n7400_1_pin11), .pin10(IMMLOE), .pin9(IMMLOE), .pin8(n7400_1_pin8));
  _74273 u_74273_6 (
    .pin1(nRST), .pin2(n74273_6_pin2), .pin3(OPCODEIMM[0]), .pin4(OPCODEIMM[1]), .pin5(n74273_6_pin5),
    .pin6(n74273_6_pin6), .pin7(OPCODEIMM[2]), .pin8(OPCODEIMM[3]), .pin9(n74273_6_pin9),
    .pin19(n74273_6_pin19), .pin18(OPCODEIMM[7]), .pin17(OPCODEIMM[6]), .pin16(n74273_6_pin16),
    .pin15(n74273_6_pin15), .pin14(OPCODEIMM[5]), .pin13(OPCODEIMM[4]), .pin12(n74273_6_pin12), .pin11(nCLK));
  IC74245 ic74245_6 (
    .DIR(1'b0), .iOE(n7400_1_pin11), .B0(n74273_6_pin2), .B1(n74273_6_pin5), .B2(n74273_6_pin6),
    .B3(n74273_6_pin9), .B4(n74273_6_pin12), .B5(n74273_6_pin15), .B6(n74273_6_pin16), .B7(n74273_6_pin19),
    .A0(IBH[0]), .A1(IBH[1]), .A2(IBH[2]), .A3(IBH[3]), .A4(IBH[4]), .A5(IBH[5]), .A6(IBH[6]), .A7(IBH[7]));
  IC74245 ic74245_7 (
    .DIR(1'b0), .iOE(n7400_1_pin8), .B0(n74273_6_pin2), .B1(n74273_6_pin5), .B2(n74273_6_pin6),
    .B3(n74273_6_pin9), .B4(n74273_6_pin12), .B5(n74273_6_pin15), .B6(n74273_6_pin16), .B7(n74273_6_pin19),
    .A0(IBL[0]), .A1(IBL[1]), .A2(IBL[2]), .A3(IBL[3]), .A4(IBL[4]), .A5(IBL[5]), .A6(IBL[6]), .A7(IBL[7]));
  // also tied to GND on the sheet: {n7432_1_pin1, n7432_1_pin13, n7432_1_pin2, n7432_1_pin12, n7414_1_pin1, n7414_1_pin13, n7474_1_pin2, n7474_1_pin12, n7474_1_pin3, n7414_1_pin11, n7474_1_pin11, n7474_2_pin1, n7474_2_pin2, n7474_2_pin3}
  // also tied to VCC on the sheet: {n7474_3_pin1, n7474_2_pin4, n7474_2_pin10, n7474_3_pin10}

  // Notes on the sheet:
  //   SIMF: pull=up
  //   nHLT: pull=up
  //   nRST: pull=up
  //   SYSCLK: pull=down
  //   AR2LE: pull=up
  //   AR2OE: pull=up
  //   BHLE: pull=up
  //   BHOE: pull=up
  //   BLLE: pull=up
  //   BLOE: pull=up
  //   EDBIE: pull=up
  //   IBHIOE: pull=up
  //   OPCODEIMM: pull=up
  //   IBLIOE: pull=up
  //   JAHLE: pull=up
  //   JALLE: pull=up
  //   PCLE: pull=up
  //   RHOE: pull=up
  //   RLOE: pull=up
  //   SFW: pull=up
  //   SNH: pull=up
  //   nRD: pull=up
  //   nWR: pull=up
  //   IBH: pull=up
  //   IBL: pull=up
  //   CFH: pull=up
  //   CFL: pull=up
  //   SFH: pull=up
  //   SFL: pull=up
  //   ZFH: pull=up
  //   ZFL: pull=up
  //   AHLE: pull=up
  //   AHOE: pull=up
  //   ALLE: pull=up
  //   ALOE: pull=up
  //   AR1CE: pull=up
  //   AR1LE: pull=up
  //   AR1OE: pull=up
  //   AR2CE: pull=up
  //   COMF: pull=up
  //   IR
  //   NOP generator
  //   contents of rom_1 (hex, n*v repeats v):
  //   0 80 20 4*0 8 1 82 22 4*2 80 20 4*0 83 23 4*3 88 28 4*8 42 12 4*2 40 10 4*0 43 13 4*3 48 18 4*8 a0
  //   a0 50 0 54 4 4 50 0 0 50 0 0 80 80 40 0 40 0 0 20 20 10 0 10 0 0 55 5 5 58 8 8 58 8 8 88 88 48 8 48
  //   8 8 28 28 18 8 18 8 8 51 1 1 81 81 41 1 41 1 1 21 21 11 1 11 1 1 90 90 80 60 50 40 60 20 50 10 5*0 8
  //   1 8 1 8 1 8 1 4*9 2 2 0 0 3 3 8 8 42 12 4*2 40 10 4*0 43 13 4*3 48 18 4*8 54 4 50 0 50 0 40 0 0 10 0
  //   0 2 2 0 0 3 3 8 8 42 12 4*2 40 10 4*0 43 13 4*3 48 18 4*8 54 4 50 0 50 0 40 0 0 10 4*0 1 1 1 0 1 0 1
  //   9 0 9 0 8 0 6
  //   DIR3
  //   DM3
  //   contents of rom_2 (hex, n*v repeats v):
  //   0 0 0 20 8 4*0 3 2 23 a 3 2 43 42 63 4a 43 42 3 2 23 a 3 2 43 42 63 4a 43 42 1 0 11 4 1 0 41 40 51
  //   44 41 40 1 0 11 4 1 0 41 40 51 44 41 40 14 0 28 28 0 14 0 80 94 80 0 14 0 10 0 20 20 0 10 0 4 0 8 8
  //   0 4 0 0 14 0 80 94 80 0 14 0 10 0 20 20 0 10 0 4 0 8 8 0 4 0 0 14 0 10 0 20 20 0 10 0 4 0 8 8 0 4 0
  //   18 10 14 24 20 24 4 14 8 18 17*0 3 2 43 42 3 2 43 42 1 0 11 4 1 0 41 40 51 44 41 40 1 0 11 4 1 0 41
  //   40 51 44 41 40 0 14 80 94 0 14 0 10 0 0 4 0 3 2 43 42 3 2 43 42 1 0 11 4 1 0 41 40 51 44 41 40 1 0
  //   11 4 1 0 41 40 51 44 41 40 0 14 80 94 0 14 0 10 0 0 4 0 0 0 8 0 0 0 4 0 0 1 8 1 0 1 4 2 4
  //   DIR2
  //   DM2
  //   contents of rom_3 (hex, n*v repeats v):
  //   5*0 40 20 0 0 0 80 0 80 40 a0 0 80 0 80 40 a0 0 80 0 80 40 a0 0 80 0 80 40 a0 0 80 0 80 8 84 0 80 0
  //   80 8 84 0 80 0 80 8 84 0 80 0 80 8 84 0 c 0 c 0 0 c 0 0 c 60 60 6c 0 8 0 8 40 40 48 0 4 0 4 20 20 24
  //   0 0 c 0 0 c 60 60 6c 0 8 0 8 40 40 48 0 4 0 4 20 20 24 60 60 6c 0 8 0 8 40 40 48 0 4 0 4 20 20 24 0
  //   20 20 0 20 20 4*40 2 3 1 0 1 4*0 4*1 0 0 1 1 40 a0 40 a0 40 a0 40 a0 0 80 0 80 8 84 0 80 0 80 8 84 0
  //   80 0 80 8 84 0 80 0 80 8 84 4*0 60 60 40 40 48 20 20 24 41 a1 41 a1 41 a1 41 a1 1 81 1 81 9 85 1 81
  //   1 81 9 85 1 81 1 81 9 85 1 81 1 81 9 85 4*1 61 61 41 41 49 21 21 25 0 0 4 2 0 2 0 2 4 0 0 2 0 2
  //   DIR1
  //   DM1
  //   contents of rom_4 (hex, n*v repeats v):
  //   0 40 20 40 20 40 20 0 0 24*10 24*8 78*0 80 80 80 0 0 0 80 80 0 0 80 80 0 80 0 80 8*90 24*88 12*80
  //   8*10 24*8 12*0 4 2 0 4 0 4 0 4 0 4 0 4 0 4 0 4
  //   DIR0
  //   DM0
  //   IMM
endmodule
