// Logisim project TalosES_CTRL_gates.circ as structural Verilog: 1 circuit, main circuit main
module main (
  input  SIMF,
  input  COMF
);

  wire and_1_out, and_3_out, CIMF, d_ff_2_q, d_ff_4_q, d_ff_4_qn, IMF, mnCLK, nCLK, nHLT, nOE, not_1_out,
       not_2_out, nRST, OMF, or_1_out, or_2_out, plarom_1_p1, plarom_1_p3, SOMF;

  D_Flip_Flop d_ff_1 (.D(1'b0), .clk(1'b0), .Q(OMF), .preset(not_1_out), .reset(or_1_out));  // open: Qn
  // PlaRom #(.Contents("2 1*8 2 1*6 2 2 1*8 2 1*5 2 1 2 1*6 2 2 1*5 0*6"), .\and (6), .outputs(1)) plarom_1: pin names not known; wires that end beside it: plarom_1_p1, plarom_1_p1, plarom_1_p3
  not not_1 (not_1_out, SOMF);
  or or_1 (or_1_out, nRST, COMF);
  and and_1 (and_1_out, plarom_1_p3, d_ff_4_qn);
  D_Flip_Flop d_ff_2 (.D(nHLT), .clk(nCLK), .Q(d_ff_2_q), .Qn(nOE), .preset(1'b1), .reset(nRST));
  not not_2 (not_2_out, SIMF);
  D_Flip_Flop d_ff_3 (.D(1'b0), .clk(1'b0), .Q(IMF), .preset(not_2_out), .reset(or_2_out));  // open: Qn
  or or_2 (or_2_out, nRST, CIMF);
  D_Flip_Flop d_ff_4 (.D(and_1_out), .clk(mnCLK), .Q(d_ff_4_q), .Qn(d_ff_4_qn), .preset(1'b1), .reset(nRST));
  and and_2 (mnCLK, nCLK, d_ff_2_q);
  and and_3 (and_3_out, d_ff_4_q, mnCLK);

  // Notes on the sheet:
  //   COMF: pull=up
  //   SIMF: pull=up
  //   opcode/imm
  //   nOE of NOP generator
  //   (this should be slightly delayed
  //   to give the IR time to latch opcode)
  //   Immediate register clock
endmodule
